# Fritzing sketch Power Controller (saved by Fritzing 0.9.6b)
circuit board: 8.47cm x 5.64444cm
breadboards: 1

parts:
  R1 = Resistor [tolerance=±5% power=0.25 resistance=1k package=THT]
  Q2 = PNP-Transistor [package="TO92 [THT]"]
  R2 = Resistor [tolerance=±5% power=0.25 resistance=1k package=THT]
  R3 = Resistor [tolerance=±5% power=0.25 resistance=220 package=THT]
  Q3 = NPN-Transistor [package="TO92 [THT]"]
  LED1 = smd LED [color="Red (633nm)" package="0805 [SMD]"]
  S1 = Round Pushbutton

nets (from the pcb view):
  N1: R1.Pin_0, S1.leg0
  N2: R1.Pin_1, Q3.B
  N3: Q2.B, R2.Pin_1
  N4: Q2.C, LED1.anode
  N5: R2.Pin_0, Q3.C
  N6: R3.Pin_0, LED1.cathode
  N7: R3.Pin_1, Q3.E
