# Fritzing sketch Step_Generator (saved by Fritzing 0.9.2b)
circuit board: 8.46667cm x 5.64444cm
breadboards: 1

parts:
  IC1 = Microchip MCP23008 8-bit I/O expander [part_number=MCP23008 package="DIP (Dual Inline) [THT]"]
  Part1 = Arduino Uno (Rev3)
  U1 = CNZ1120 [package=cnz1120]
  U2 = CNZ1120 [package=cnz1120]
  U3 = CNZ1120 [package=cnz1120]
  R1 = Resistor [tolerance=±5% resistance=220 package=THT]

nets:
  N1: IC1.SCL, Part1.A5/SCL
  N2: IC1.SDA, Part1.A4/SDA
  VSS: IC1.A2, IC1.A1, IC1.A0, IC1.VSS, Part1.GND, U1.2, U1.3, U2.2, U2.3, U3.2, U3.3
  VDD: IC1.Reset, IC1.VDD, Part1.5V, R1.Pin_1
  N3: IC1.GP0, U3.4
  N4: IC1.GP1, U2.4
  N5: IC1.GP2, U1.4
  N6: U1.1, U2.1, U3.1, R1.Pin_0

custom parts:
  Microchip MCP23008 8-bit I/O expander: Provides 8-bit, general purpose, parallel I/O expansion for I2C bus. Datasheet: http://ww1.microchip.com/downloads/en/devicedoc/21919e.pdf
