# Fritzing sketch Untitled Sketch 3 (saved by Fritzing 0.9.2b)
circuit board: 8.46667cm x 5.64444cm
breadboards: 1

parts:
  U2 = CNZ1120 [package=cnz1120]
  U3 = CNZ1120 [package=cnz1120]
  U4 = CNZ1120 [package=cnz1120]
  R1 = Resistor [tolerance=±5% resistance=220 package=THT]
  IC2 = Microchip MCP23008 8-bit I/O expander [part_number=MCP23008 package="DIP (Dual Inline) [THT]"]
  Part1 = Arduino Uno (Rev3)

nets:
  N1: U2.1, U3.1, U4.1, R1.Pin_0
  GND: U2.2, U2.3, U3.2, U3.3, U4.2, U4.3, IC2.A2, IC2.A1, IC2.A0, IC2.VSS, Part1.GND
  N2: U2.4, IC2.GP0
  N3: U3.4, IC2.GP1
  N4: U4.4, IC2.GP2
  VDD: R1.Pin_1, IC2.Reset, IC2.VDD, Part1.5V
  N5: IC2.SCL, Part1.A5/SCL
  N6: IC2.SDA, Part1.A4/SDA

custom parts:
  Microchip MCP23008 8-bit I/O expander: Provides 8-bit, general purpose, parallel I/O expansion for I2C bus. Datasheet: http://ww1.microchip.com/downloads/en/devicedoc/21919e.pdf
